// Logisim project simon_says.circ as structural Verilog: 1 circuit, main circuit main
module main (
);

  wire and_1_out, and_2_out, and_3_out, and_4_out, and_5_out, and_6_out, and_7_out, and_8_out, and_9_out,
       clock_1_out, dipswitch_1_p1, dipswitch_1_p2, dipswitch_1_p3, dipswitch_1_p4, dipswitch_2_p1,
       dipswitch_2_p2, dipswitch_2_p3, dipswitch_2_p4, dipswitch_3_p2, dipswitch_3_p3, dipswitch_3_p4,
       dipswitch_3_p5, dipswitch_4_p1, dipswitch_4_p2, dipswitch_4_p3, dipswitch_4_p4, j_k_ff_1_q,
       j_k_ff_2_q, j_k_ff_3_q, j_k_ff_4_q, j_k_ff_5_q, j_k_ff_6_q, register_1_q, register_2_q, register_3_q,
       register_4_q, register_5_q, register_6_q, register_7_q, register_8_q, register_10_q, register_11_q,
       register_12_q, register_13_q, register_14_q, register_15_q, register_16_q, undriven, undriven_2,
       undriven_3, xnor_1_out, xnor_2_out, xnor_3_out, xnor_4_out, xnor_5_out, xnor_6_out, xnor_7_out,
       xnor_8_out, xnor_9_out, xnor_10_out, xnor_11_out, xnor_12_out;

  Clock clock_1 (.out(clock_1_out));
  Register #(.width(1)) register_1 (.D(dipswitch_1_p1), .en(1'b1), .clk(clock_1_out), .Q(register_1_q), .clr(1'b0));
  Register #(.width(1)) register_2 (.D(dipswitch_2_p1), .en(1'b1), .clk(clock_1_out), .Q(register_2_q), .clr(1'b0));
  Register #(.width(1)) register_3 (.D(dipswitch_3_p2), .en(1'b1), .clk(clock_1_out), .Q(register_3_q), .clr(1'b0));
  Register #(.width(1)) register_4 (.D(dipswitch_4_p1), .en(1'b1), .clk(clock_1_out), .Q(register_4_q), .clr(1'b0));
  // DipSwitch #(.number(4)) dipswitch_1: pin names not known; wires that end beside it: dipswitch_1_p1, dipswitch_1_p2, dipswitch_1_p3, dipswitch_1_p4
  // DipSwitch #(.number(4)) dipswitch_2: pin names not known; wires that end beside it: dipswitch_2_p1, dipswitch_2_p2, dipswitch_2_p3, dipswitch_2_p4
  // DipSwitch #(.number(4)) dipswitch_3: pin names not known; wires that end beside it: 1'b1, dipswitch_3_p2, dipswitch_3_p3, dipswitch_3_p4, dipswitch_3_p5
  xnor xnor_1 (xnor_1_out, register_1_q, register_4_q);
  Register #(.width(1)) register_5 (.D(dipswitch_1_p2), .en(1'b1), .clk(clock_1_out), .Q(register_5_q), .clr(1'b0));
  xnor xnor_2 (xnor_2_out, register_1_q, register_2_q);
  Register #(.width(1)) register_6 (.D(dipswitch_2_p2), .en(1'b1), .clk(clock_1_out), .Q(register_6_q), .clr(1'b0));
  xnor xnor_3 (xnor_3_out, register_1_q, register_3_q);
  Register #(.width(1)) register_7 (.D(dipswitch_3_p3), .en(1'b1), .clk(clock_1_out), .Q(register_7_q), .clr(1'b0));
  // DipSwitch #(.number(4)) dipswitch_4: pin names not known; wires that end beside it: dipswitch_4_p1, dipswitch_4_p2, dipswitch_4_p3, dipswitch_4_p4
  Register #(.width(1)) register_8 (.D(dipswitch_4_p2), .en(1'b1), .clk(clock_1_out), .Q(register_8_q), .clr(1'b0));
  xnor xnor_4 (xnor_4_out, register_5_q, register_6_q);
  Register #(.width(1)) register_9 (.D(dipswitch_2_p3), .en(1'b1), .clk(clock_1_out), .Q(dipswitch_2_p4), .clr(1'b0));
  xnor xnor_5 (xnor_5_out, register_5_q, register_7_q);
  Register #(.width(1)) register_10 (.D(dipswitch_3_p4), .en(1'b1), .clk(clock_1_out), .Q(register_10_q), .clr(1'b0));
  xnor xnor_6 (xnor_6_out, register_5_q, register_8_q);
  Register #(.width(1)) register_11 (.D(dipswitch_1_p3), .en(1'b1), .clk(clock_1_out), .Q(register_11_q), .clr(1'b0));
  and and_1 (and_1_out, xnor_4_out, xnor_2_out);
  and and_2 (and_2_out, xnor_5_out, xnor_3_out);
  and and_3 (and_3_out, xnor_6_out, xnor_1_out);
  Register #(.width(1)) register_12 (.D(dipswitch_4_p3), .en(1'b1), .clk(clock_1_out), .Q(register_12_q), .clr(1'b0));
  Register #(.width(1)) register_13 (.D(dipswitch_1_p4), .en(1'b1), .clk(clock_1_out), .Q(register_13_q), .clr(1'b0));
  xnor xnor_7 (xnor_7_out, register_11_q, dipswitch_2_p4);
  Register #(.width(1)) register_14 (.D(dipswitch_2_p4), .en(1'b1), .clk(clock_1_out), .Q(register_14_q), .clr(1'b0));
  xnor xnor_8 (xnor_8_out, register_11_q, register_10_q);
  Register #(.width(1)) register_15 (.D(dipswitch_3_p5), .en(1'b1), .clk(clock_1_out), .Q(register_15_q), .clr(1'b0));
  xnor xnor_9 (xnor_9_out, register_11_q, register_12_q);
  and and_4 (and_4_out, xnor_7_out, and_1_out);
  and and_5 (and_5_out, xnor_8_out, and_2_out);
  and and_6 (and_6_out, xnor_9_out, and_3_out);
  Register #(.width(1)) register_16 (.D(dipswitch_4_p4), .en(1'b1), .clk(clock_1_out), .Q(register_16_q), .clr(1'b0));
  xnor xnor_10 (xnor_10_out, register_13_q, register_14_q);
  xnor xnor_11 (xnor_11_out, register_13_q, register_15_q);
  xnor xnor_12 (xnor_12_out, register_13_q, register_16_q);
  and and_7 (and_7_out, xnor_10_out, and_4_out);
  and and_8 (and_8_out, xnor_11_out, and_5_out);
  and and_9 (and_9_out, xnor_12_out, and_6_out);
  J_K_Flip_Flop j_k_ff_1 (
    .J(undriven_3), .K(undriven_3), .clk(and_7_out), .Q(j_k_ff_1_q), .preset(undriven_3), .reset(1'b0));  // open: Qn
  J_K_Flip_Flop j_k_ff_2 (
    .J(undriven), .K(undriven), .clk(and_8_out), .Q(j_k_ff_2_q), .preset(undriven), .reset(1'b0));  // open: Qn
  J_K_Flip_Flop j_k_ff_3 (
    .J(undriven_2), .K(undriven_2), .clk(and_9_out), .Q(j_k_ff_3_q), .preset(undriven_2), .reset(1'b0));  // open: Qn
  LED led_1 (.in(j_k_ff_1_q));
  LED led_2 (.in(j_k_ff_2_q));
  J_K_Flip_Flop j_k_ff_4 (
    .J(1'b1), .K(1'b1), .clk(j_k_ff_2_q), .Q(j_k_ff_4_q), .preset(undriven), .reset(1'b0));  // open: Qn
  LED led_3 (.in(j_k_ff_3_q));
  J_K_Flip_Flop j_k_ff_5 (
    .J(1'b1), .K(1'b1), .clk(j_k_ff_3_q), .Q(j_k_ff_5_q), .preset(undriven_2), .reset(1'b0));  // open: Qn
  LED led_4 (.in(j_k_ff_6_q));
  J_K_Flip_Flop j_k_ff_6 (
    .J(1'b1), .K(1'b1), .clk(j_k_ff_1_q), .Q(j_k_ff_6_q), .preset(undriven_3), .reset(1'b0));  // open: Qn
  LED led_5 (.in(j_k_ff_4_q));
  LED led_6 (.in(j_k_ff_5_q));

  // Notes on the sheet:
  //   User
  //   Simon
endmodule
